# Fritzing sketch noise_monitor (saved by Fritzing 0.9.9b)
breadboards: 1

parts:
  LED2 = smd LED [color="Blue (430nm)" package="0805 [SMD]"]
  LED3 = smd LED [color="Green (555nm)" package="0805 [SMD]"]
  IC1 = Amica NodeMCU DevKit 1.0
  ResetSW = Pushbutton [package="[SMD]"]
  TRS1 = Audio Jack (TRS) 3.5mm [package="PG203J [THT]"]
  R1 = Resistor [tolerance=±10% resistance=220 package="2010 [SMD]"]
  R2 = Resistor [tolerance=±10% resistance=220 package="2010 [SMD]"]
  R3 = Trimmer Potentiometer [maximum_resistance=100kΩ package=THT]
  C1 = Electrolytic Capacitor [capacitance=47µF voltage=50V package="0807 [SMD, electrolytic]"]
  D1 = Rectifier Diode [part_number=1N4148 package="Melf DO-213 AB [SMD]"]

nets:
  N1: LED2.cathode, IC1.pin7
  N2: LED2.anode, R2.Pin_1
  N3: LED3.cathode, IC1.pin8
  N4: LED3.anode, R1.Pin_1
  N5: IC1.pin1, IC1.pin_10, IC1.pin_26
  GND: IC1.pin2, IC1.pin_9, IC1.pin_25, IC1.pin_29, ResetSW.Pin_3, ResetSW.Pin_4, TRS1.Sleeve, R1.Pin_0, R2.Pin_0, R3.wiper, C1.-
  N6: IC1.pin_14, ResetSW.Pin_1, ResetSW.Pin_2
  N7: IC1.pin_16, R3.leg2, C1.+, D1.cathode
  N8: TRS1.Tip, D1.anode

custom parts:
  Amica NodeMCU DevKit 1.0: Amica NodeMCU DevKit 1.0 Development Kit based on ESP8266 ESP-12E, integating GPIO, PWM, IIC, 1-Wire and ADC all in one board. Links: NodeMCU information page Github
